// Logisim project 8BitPC.circ as structural Verilog: 1 circuit, main circuit main
module main (
  input  in_1,
  input  in_2,
  input  in_3,
  input  in_4,
  input  in_5,
  input  in_6,
  input  in_7,
  input  in_8,
  input  in_9,
  input  in_10,
  input  in_11,
  input  in_12,
  input  in_13,
  input  in_14,
  input  in_15,
  input  Data,
  input  in_17,
  input  in_18,
  input  in_19,
  input  in_20,
  input  in_21,
  input  Load,
  input  Load_2,
  input  Load_3,
  input  in_25,
  input  Address,
  input  in_27,
  input  in_28,
  input  in_29,
  input  in_30,
  input  Address_mode,
  input  Write,
  input  in_33
);

  wire and_1_out, and_2_out, and_3_out, and_4_out, and_5_out, and_6_out, and_7_out, and_8_out, and_9_out,
       and_10_out, and_11_out, and_12_out, and_13_out, and_14_out, and_15_out, and_16_out, and_17_out,
       and_18_out, and_19_out, and_20_out, and_21_out, and_22_out, and_23_out, and_24_out, and_25_out,
       and_26_out, and_27_out, and_28_out, and_29_out, and_30_out, and_31_out, and_32_out, and_33_out,
       and_34_out, and_35_out, and_36_out, and_37_out, and_38_out, and_39_out, and_40_out, and_41_out,
       and_42_out, and_43_out, and_44_out, and_45_out, and_46_out, and_47_out, and_48_out, and_49_out,
       and_50_out, and_51_out, and_52_out, and_53_out, and_54_out, and_55_out, and_56_out, and_57_out,
       and_58_out, and_59_out, and_60_out, and_61_out, and_62_out, and_63_out, and_64_out, and_65_out,
       and_66_out, and_67_out, and_68_out, and_69_out, and_70_out, and_71_out, and_72_out, and_73_out,
       and_74_out, and_75_out, and_76_out, and_77_out, and_78_out, and_79_out, and_80_out, and_81_out,
       and_82_out, and_83_out, and_84_out, and_85_out, and_86_out, and_87_out, and_88_out, and_89_out,
       and_90_out, and_91_out, and_92_out, and_93_out, and_94_out, and_95_out, and_96_out, and_97_out,
       and_98_out, and_99_out, and_100_out, and_101_out, and_102_out, and_103_out, and_104_out, and_105_out,
       and_106_out, and_107_out, and_108_out, and_109_out, and_110_out, and_111_out, and_112_out,
       and_113_out, and_114_out, and_115_out, and_116_out, and_117_out, and_118_out, and_119_out,
       and_120_out, and_121_out, and_122_out, and_123_out, and_124_out, and_125_out, and_126_out,
       and_127_out, and_128_out, and_129_out, and_130_out, and_131_out, and_132_out, and_133_out,
       and_134_out, and_135_out, and_136_out, and_137_out, clock_1_out, controlled_buffer_5_out,
       controlled_buffer_6_out, controlled_buffer_7_out, nor_2_out, nor_4_out, nor_6_out, nor_8_out,
       nor_10_out, nor_12_out, nor_14_out, nor_16_out, nor_18_out, nor_20_out, nor_22_out, nor_24_out,
       nor_26_out, nor_28_out, nor_30_out, nor_32_out, nor_34_out, nor_36_out, nor_38_out, nor_40_out,
       nor_42_out, nor_44_out, nor_46_out, nor_48_out, nor_49_out, nor_50_out, nor_51_out, nor_52_out,
       nor_53_out, nor_54_out, nor_55_out, nor_56_out, not_1_out, not_2_out, not_3_out, not_4_out, not_5_out,
       not_6_out, not_7_out, not_8_out, not_9_out, not_10_out, not_11_out, not_12_out, not_13_out,
       not_14_out, not_15_out, not_16_out, not_17_out, not_18_out, not_19_out, not_20_out, not_21_out,
       not_22_out, not_23_out, not_24_out, not_25_out, not_26_out, not_27_out, not_28_out, not_29_out,
       not_30_out, not_31_out, not_32_out, not_33_out, not_34_out, not_35_out, not_36_out, not_37_out,
       not_38_out, not_39_out, not_40_out, not_41_out, not_42_out, not_43_out, not_44_out, not_45_out,
       not_46_out, not_47_out, not_48_out, not_49_out, not_50_out, not_51_out, not_52_out, not_53_out,
       not_54_out, not_55_out, not_56_out, not_57_out, not_58_out, not_59_out, not_60_out, or_1_out,
       or_2_out, or_3_out, or_4_out, or_5_out, or_6_out, or_7_out, or_8_out, or_9_out, or_10_out, or_11_out,
       or_12_out, or_13_out, or_14_out, or_15_out, or_16_out, or_17_out, or_18_out, or_19_out, or_20_out,
       or_21_out, or_22_out, or_23_out, or_24_out, or_25_out, or_26_out, or_27_out, or_28_out, or_29_out,
       or_30_out, or_31_out, or_32_out, or_33_out, or_34_out, or_35_out, or_36_out, undriven, undriven_2,
       undriven_3, undriven_4, xor_1_out, xor_2_out, xor_3_out, xor_4_out, xor_5_out, xor_6_out, xor_7_out,
       xor_8_out, xor_9_out, xor_10_out, xor_11_out, xor_12_out, xor_13_out, xor_14_out, xor_15_out,
       xor_16_out;
  wire [3:0] nor_1_out, nor_9_out, nor_17_out, nor_25_out, nor_39_out, nor_47_out, or_37_out;
  wire [7:0] controlled_buffer_1_out, ram_1_dout, xor_20_out;

  Clock clock_1 (.out(clock_1_out));
  assign controlled_buffer_1_out = in_1 ? {in_15, in_14, in_11, in_10, in_9, in_5, in_3, in_2} : 8'bz;  // Controlled_Buffer controlled_buffer_1
  not not_1 (not_1_out, clock_1_out);
  not not_2 (not_2_out, not_1_out);
  not not_3 (not_3_out, not_2_out);
  and and_1 (and_1_out, clock_1_out, not_3_out);
  not not_4 (not_4_out, Load);
  not not_5 (not_5_out, Load);
  not not_6 (not_6_out, Load);
  not not_7 (not_7_out, Load);
  not not_8 (not_8_out, Load);
  not not_9 (not_9_out, Load);
  not not_10 (not_10_out, Load);
  not not_11 (not_11_out, Load);
  and and_2 (and_2_out, nor_1_out[3], not_4_out);
  and and_3 (and_3_out, Load, controlled_buffer_1_out[0]);
  and and_4 (and_4_out, nor_1_out[2], not_5_out);
  and and_5 (and_5_out, Load, controlled_buffer_1_out[1]);
  and and_6 (and_6_out, nor_1_out[1], not_6_out);
  and and_7 (and_7_out, Load, controlled_buffer_1_out[2]);
  and and_8 (and_8_out, nor_1_out[0], not_7_out);
  and and_9 (and_9_out, Load, controlled_buffer_1_out[3]);
  and and_10 (and_10_out, nor_9_out[3], not_8_out);
  and and_11 (and_11_out, Load, controlled_buffer_1_out[4]);
  and and_12 (and_12_out, nor_9_out[2], not_9_out);
  and and_13 (and_13_out, Load, controlled_buffer_1_out[5]);
  and and_14 (and_14_out, nor_9_out[1], not_10_out);
  and and_15 (and_15_out, Load, controlled_buffer_1_out[6]);
  and and_16 (and_16_out, nor_9_out[0], not_11_out);
  and and_17 (and_17_out, Load, controlled_buffer_1_out[7]);
  or or_1 (or_1_out, and_2_out, and_3_out);
  or or_2 (or_2_out, and_4_out, and_5_out);
  or or_3 (or_3_out, and_6_out, and_7_out);
  or or_4 (or_4_out, and_8_out, and_9_out);
  or or_5 (or_5_out, and_10_out, and_11_out);
  or or_6 (or_6_out, and_12_out, and_13_out);
  or or_7 (or_7_out, and_14_out, and_15_out);
  or or_8 (or_8_out, and_16_out, and_17_out);
  not not_12 (not_12_out, or_1_out);
  not not_13 (not_13_out, or_2_out);
  not not_14 (not_14_out, or_3_out);
  not not_15 (not_15_out, or_4_out);
  not not_16 (not_16_out, or_5_out);
  not not_17 (not_17_out, or_6_out);
  not not_18 (not_18_out, or_7_out);
  not not_19 (not_19_out, or_8_out);
  and and_18 (and_18_out, not_12_out, and_1_out);
  and and_19 (and_19_out, and_1_out, or_1_out);
  and and_20 (and_20_out, not_13_out, and_1_out);
  and and_21 (and_21_out, and_1_out, or_2_out);
  and and_22 (and_22_out, not_14_out, and_1_out);
  and and_23 (and_23_out, and_1_out, or_3_out);
  and and_24 (and_24_out, not_15_out, and_1_out);
  and and_25 (and_25_out, and_1_out, or_4_out);
  and and_26 (and_26_out, not_16_out, and_1_out);
  and and_27 (and_27_out, and_1_out, or_5_out);
  and and_28 (and_28_out, not_17_out, and_1_out);
  and and_29 (and_29_out, and_1_out, or_6_out);
  and and_30 (and_30_out, not_18_out, and_1_out);
  and and_31 (and_31_out, and_1_out, or_7_out);
  and and_32 (and_32_out, not_19_out, and_1_out);
  and and_33 (and_33_out, and_1_out, or_8_out);
  nor nor_1 (nor_1_out[3], and_18_out, nor_2_out);
  nor nor_2 (nor_2_out, nor_1_out[3], and_19_out);
  nor nor_3 (nor_1_out[2], and_20_out, nor_4_out);
  nor nor_4 (nor_4_out, nor_1_out[2], and_21_out);
  nor nor_5 (nor_1_out[1], and_22_out, nor_6_out);
  nor nor_6 (nor_6_out, nor_1_out[1], and_23_out);
  nor nor_7 (nor_1_out[0], and_24_out, nor_8_out);
  nor nor_8 (nor_8_out, nor_1_out[0], and_25_out);
  nor nor_9 (nor_9_out[3], and_26_out, nor_10_out);
  nor nor_10 (nor_10_out, nor_9_out[3], and_27_out);
  nor nor_11 (nor_9_out[2], and_28_out, nor_12_out);
  nor nor_12 (nor_12_out, nor_9_out[2], and_29_out);
  nor nor_13 (nor_9_out[1], and_30_out, nor_14_out);
  nor nor_14 (nor_14_out, nor_9_out[1], and_31_out);
  nor nor_15 (nor_9_out[0], and_32_out, nor_16_out);
  nor nor_16 (nor_16_out, nor_9_out[0], and_33_out);
  Hex_Digit_Display hex_digit_display_1 (.value(nor_1_out));  // open: dp
  Hex_Digit_Display hex_digit_display_2 (.value(nor_9_out));  // open: dp
  assign controlled_buffer_1_out = in_6 ? {nor_9_out[0], nor_9_out[1], nor_9_out[2], nor_9_out[3], nor_1_out[0], nor_1_out[1], nor_1_out[2], nor_1_out[3]} : 8'bz;  // Controlled_Buffer controlled_buffer_2
  not not_20 (not_20_out, Load_2);
  not not_21 (not_21_out, Load_2);
  not not_22 (not_22_out, Load_2);
  not not_23 (not_23_out, Load_2);
  not not_24 (not_24_out, Load_2);
  not not_25 (not_25_out, Load_2);
  not not_26 (not_26_out, Load_2);
  not not_27 (not_27_out, Load_2);
  and and_34 (and_34_out, nor_17_out[3], not_20_out);
  and and_35 (and_35_out, Load_2, controlled_buffer_1_out[0]);
  and and_36 (and_36_out, nor_17_out[2], not_21_out);
  and and_37 (and_37_out, Load_2, controlled_buffer_1_out[1]);
  and and_38 (and_38_out, nor_17_out[1], not_22_out);
  and and_39 (and_39_out, Load_2, controlled_buffer_1_out[2]);
  and and_40 (and_40_out, nor_17_out[0], not_23_out);
  and and_41 (and_41_out, Load_2, controlled_buffer_1_out[3]);
  and and_42 (and_42_out, nor_25_out[3], not_24_out);
  and and_43 (and_43_out, Load_2, controlled_buffer_1_out[4]);
  and and_44 (and_44_out, nor_25_out[2], not_25_out);
  and and_45 (and_45_out, Load_2, controlled_buffer_1_out[5]);
  and and_46 (and_46_out, nor_25_out[1], not_26_out);
  and and_47 (and_47_out, Load_2, controlled_buffer_1_out[6]);
  and and_48 (and_48_out, nor_25_out[0], not_27_out);
  and and_49 (and_49_out, Load_2, controlled_buffer_1_out[7]);
  or or_9 (or_9_out, and_34_out, and_35_out);
  or or_10 (or_10_out, and_36_out, and_37_out);
  or or_11 (or_11_out, and_38_out, and_39_out);
  or or_12 (or_12_out, and_40_out, and_41_out);
  or or_13 (or_13_out, and_42_out, and_43_out);
  or or_14 (or_14_out, and_44_out, and_45_out);
  or or_15 (or_15_out, and_46_out, and_47_out);
  or or_16 (or_16_out, and_48_out, and_49_out);
  not not_28 (not_28_out, or_9_out);
  not not_29 (not_29_out, or_10_out);
  not not_30 (not_30_out, or_11_out);
  not not_31 (not_31_out, or_12_out);
  not not_32 (not_32_out, or_13_out);
  not not_33 (not_33_out, or_14_out);
  not not_34 (not_34_out, or_15_out);
  not not_35 (not_35_out, or_16_out);
  and and_50 (and_50_out, not_28_out, and_1_out);
  and and_51 (and_51_out, and_1_out, or_9_out);
  and and_52 (and_52_out, not_29_out, and_1_out);
  and and_53 (and_53_out, and_1_out, or_10_out);
  and and_54 (and_54_out, not_30_out, and_1_out);
  and and_55 (and_55_out, and_1_out, or_11_out);
  and and_56 (and_56_out, not_31_out, and_1_out);
  and and_57 (and_57_out, and_1_out, or_12_out);
  and and_58 (and_58_out, not_32_out, and_1_out);
  and and_59 (and_59_out, and_1_out, or_13_out);
  and and_60 (and_60_out, not_33_out, and_1_out);
  and and_61 (and_61_out, and_1_out, or_14_out);
  and and_62 (and_62_out, not_34_out, and_1_out);
  and and_63 (and_63_out, and_1_out, or_15_out);
  and and_64 (and_64_out, not_35_out, and_1_out);
  and and_65 (and_65_out, and_1_out, or_16_out);
  nor nor_17 (nor_17_out[3], and_50_out, nor_18_out);
  nor nor_18 (nor_18_out, nor_17_out[3], and_51_out);
  nor nor_19 (nor_17_out[2], and_52_out, nor_20_out);
  nor nor_20 (nor_20_out, nor_17_out[2], and_53_out);
  nor nor_21 (nor_17_out[1], and_54_out, nor_22_out);
  nor nor_22 (nor_22_out, nor_17_out[1], and_55_out);
  nor nor_23 (nor_17_out[0], and_56_out, nor_24_out);
  nor nor_24 (nor_24_out, nor_17_out[0], and_57_out);
  nor nor_25 (nor_25_out[3], and_58_out, nor_26_out);
  nor nor_26 (nor_26_out, nor_25_out[3], and_59_out);
  nor nor_27 (nor_25_out[2], and_60_out, nor_28_out);
  nor nor_28 (nor_28_out, nor_25_out[2], and_61_out);
  nor nor_29 (nor_25_out[1], and_62_out, nor_30_out);
  nor nor_30 (nor_30_out, nor_25_out[1], and_63_out);
  nor nor_31 (nor_25_out[0], and_64_out, nor_32_out);
  nor nor_32 (nor_32_out, nor_25_out[0], and_65_out);
  Hex_Digit_Display hex_digit_display_3 (.value(nor_17_out));  // open: dp
  Hex_Digit_Display hex_digit_display_4 (.value(nor_25_out));  // open: dp
  assign controlled_buffer_1_out = in_7 ? {nor_25_out[0], nor_25_out[1], nor_25_out[2], nor_25_out[3], nor_17_out[0], nor_17_out[1], nor_17_out[2], nor_17_out[3]} : 8'bz;  // Controlled_Buffer controlled_buffer_3
  not not_36 (not_36_out, Load_3);
  not not_37 (not_37_out, Load_3);
  not not_38 (not_38_out, Load_3);
  not not_39 (not_39_out, Load_3);
  not not_40 (not_40_out, Load_3);
  not not_41 (not_41_out, Load_3);
  not not_42 (not_42_out, Load_3);
  not not_43 (not_43_out, Load_3);
  and and_66 (and_66_out, nor_39_out[3], not_36_out);
  and and_67 (and_67_out, Load_3, controlled_buffer_1_out[0]);
  and and_68 (and_68_out, nor_39_out[2], not_37_out);
  and and_69 (and_69_out, Load_3, controlled_buffer_1_out[1]);
  and and_70 (and_70_out, nor_39_out[1], not_38_out);
  and and_71 (and_71_out, Load_3, controlled_buffer_1_out[2]);
  and and_72 (and_72_out, nor_39_out[0], not_39_out);
  and and_73 (and_73_out, Load_3, controlled_buffer_1_out[3]);
  and and_74 (and_74_out, nor_47_out[3], not_40_out);
  and and_75 (and_75_out, Load_3, controlled_buffer_1_out[4]);
  and and_76 (and_76_out, nor_47_out[2], not_41_out);
  and and_77 (and_77_out, Load_3, controlled_buffer_1_out[5]);
  and and_78 (and_78_out, nor_47_out[1], not_42_out);
  and and_79 (and_79_out, Load_3, controlled_buffer_1_out[6]);
  and and_80 (and_80_out, nor_47_out[0], not_43_out);
  and and_81 (and_81_out, Load_3, controlled_buffer_1_out[7]);
  or or_17 (or_17_out, and_66_out, and_67_out);
  or or_18 (or_18_out, and_68_out, and_69_out);
  or or_19 (or_19_out, and_70_out, and_71_out);
  or or_20 (or_20_out, and_72_out, and_73_out);
  or or_21 (or_21_out, and_74_out, and_75_out);
  or or_22 (or_22_out, and_76_out, and_77_out);
  or or_23 (or_23_out, and_78_out, and_79_out);
  or or_24 (or_24_out, and_80_out, and_81_out);
  not not_44 (not_44_out, or_17_out);
  not not_45 (not_45_out, or_18_out);
  not not_46 (not_46_out, or_19_out);
  not not_47 (not_47_out, or_20_out);
  not not_48 (not_48_out, or_21_out);
  not not_49 (not_49_out, or_22_out);
  not not_50 (not_50_out, or_23_out);
  not not_51 (not_51_out, or_24_out);
  and and_82 (and_82_out, not_44_out, and_1_out);
  and and_83 (and_83_out, and_1_out, or_17_out);
  and and_84 (and_84_out, not_45_out, and_1_out);
  and and_85 (and_85_out, and_1_out, or_18_out);
  and and_86 (and_86_out, not_46_out, and_1_out);
  and and_87 (and_87_out, and_1_out, or_19_out);
  and and_88 (and_88_out, not_47_out, and_1_out);
  and and_89 (and_89_out, and_1_out, or_20_out);
  and and_90 (and_90_out, not_48_out, and_1_out);
  and and_91 (and_91_out, and_1_out, or_21_out);
  and and_92 (and_92_out, not_49_out, and_1_out);
  and and_93 (and_93_out, and_1_out, or_22_out);
  and and_94 (and_94_out, not_50_out, and_1_out);
  and and_95 (and_95_out, and_1_out, or_23_out);
  and and_96 (and_96_out, not_51_out, and_1_out);
  and and_97 (and_97_out, and_1_out, or_24_out);
  nor nor_33 (nor_39_out[3], and_82_out, nor_34_out);
  nor nor_34 (nor_34_out, nor_39_out[3], and_83_out);
  nor nor_35 (nor_39_out[2], and_84_out, nor_36_out);
  nor nor_36 (nor_36_out, nor_39_out[2], and_85_out);
  nor nor_37 (nor_39_out[1], and_86_out, nor_38_out);
  nor nor_38 (nor_38_out, nor_39_out[1], and_87_out);
  nor nor_39 (nor_39_out[0], and_88_out, nor_40_out);
  nor nor_40 (nor_40_out, nor_39_out[0], and_89_out);
  nor nor_41 (nor_47_out[3], and_90_out, nor_42_out);
  nor nor_42 (nor_42_out, nor_47_out[3], and_91_out);
  nor nor_43 (nor_47_out[2], and_92_out, nor_44_out);
  nor nor_44 (nor_44_out, nor_47_out[2], and_93_out);
  nor nor_45 (nor_47_out[1], and_94_out, nor_46_out);
  nor nor_46 (nor_46_out, nor_47_out[1], and_95_out);
  nor nor_47 (nor_47_out[0], and_96_out, nor_48_out);
  nor nor_48 (nor_48_out, nor_47_out[0], and_97_out);
  Hex_Digit_Display hex_digit_display_5 (.value(nor_39_out));  // open: dp
  Hex_Digit_Display hex_digit_display_6 (.value(nor_47_out));  // open: dp
  Controlled_Buffer controlled_buffer_4 (.in(nor_39_out[3]), .en(in_8));  // open: out
  assign controlled_buffer_5_out = in_8 ? nor_39_out[2] : 1'bz;  // Controlled_Buffer controlled_buffer_5
  assign controlled_buffer_6_out = in_8 ? nor_39_out[1] : 1'bz;  // Controlled_Buffer controlled_buffer_6
  assign controlled_buffer_7_out = in_8 ? nor_39_out[0] : 1'bz;  // Controlled_Buffer controlled_buffer_7
  assign controlled_buffer_1_out[4] = in_8 ? nor_47_out[3] : 1'bz;  // Controlled_Buffer controlled_buffer_8
  assign controlled_buffer_1_out[5] = in_8 ? nor_47_out[2] : 1'bz;  // Controlled_Buffer controlled_buffer_9
  assign controlled_buffer_1_out[6] = in_8 ? nor_47_out[1] : 1'bz;  // Controlled_Buffer controlled_buffer_10
  assign controlled_buffer_1_out[7] = in_8 ? nor_47_out[0] : 1'bz;  // Controlled_Buffer controlled_buffer_11
  assign controlled_buffer_1_out[0] = in_8 ? 1'b0 : 1'bz;  // Controlled_Buffer controlled_buffer_12
  assign controlled_buffer_1_out[1] = in_8 ? 1'b0 : 1'bz;  // Controlled_Buffer controlled_buffer_13
  assign controlled_buffer_1_out[2] = in_8 ? 1'b0 : 1'bz;  // Controlled_Buffer controlled_buffer_14
  assign controlled_buffer_1_out[3] = in_8 ? 1'b0 : 1'bz;  // Controlled_Buffer controlled_buffer_15
  xor xor_1 (xor_1_out, nor_17_out[3], in_33);
  xor xor_2 (xor_2_out, nor_17_out[2], in_33);
  xor xor_3 (xor_3_out, nor_17_out[1], in_33);
  xor xor_4 (xor_4_out, nor_17_out[0], in_33);
  xor xor_5 (xor_5_out, nor_25_out[3], in_33);
  xor xor_6 (xor_6_out, nor_25_out[2], in_33);
  xor xor_7 (xor_7_out, nor_25_out[1], in_33);
  xor xor_8 (xor_8_out, nor_25_out[0], in_33);
  xor xor_9 (xor_9_out, nor_1_out[3], xor_1_out);
  and and_98 (and_98_out, or_26_out, xor_9_out);
  and and_99 (and_99_out, nor_1_out[3], xor_1_out);
  xor xor_10 (xor_10_out, nor_1_out[2], xor_2_out);
  and and_100 (and_100_out, or_27_out, xor_10_out);
  and and_101 (and_101_out, nor_1_out[2], xor_2_out);
  xor xor_11 (xor_11_out, nor_1_out[1], xor_3_out);
  and and_102 (and_102_out, or_28_out, xor_11_out);
  and and_103 (and_103_out, nor_1_out[1], xor_3_out);
  xor xor_12 (xor_12_out, nor_1_out[0], xor_4_out);
  and and_104 (and_104_out, or_29_out, xor_12_out);
  and and_105 (and_105_out, nor_1_out[0], xor_4_out);
  xor xor_13 (xor_13_out, nor_9_out[3], xor_5_out);
  and and_106 (and_106_out, or_30_out, xor_13_out);
  and and_107 (and_107_out, nor_9_out[3], xor_5_out);
  xor xor_14 (xor_14_out, nor_9_out[2], xor_6_out);
  and and_108 (and_108_out, or_31_out, xor_14_out);
  and and_109 (and_109_out, nor_9_out[2], xor_6_out);
  xor xor_15 (xor_15_out, nor_9_out[1], xor_7_out);
  and and_110 (and_110_out, or_32_out, xor_15_out);
  and and_111 (and_111_out, nor_9_out[1], xor_7_out);
  xor xor_16 (xor_16_out, nor_9_out[0], xor_8_out);
  and and_112 (and_112_out, in_33, xor_16_out);
  and and_113 (and_113_out, nor_9_out[0], xor_8_out);
  xor xor_17 (xor_20_out[0], xor_9_out, or_26_out);
  or or_25 (or_25_out, and_98_out, and_99_out);
  xor xor_18 (xor_20_out[1], xor_10_out, or_27_out);
  or or_26 (or_26_out, and_100_out, and_101_out);
  xor xor_19 (xor_20_out[2], xor_11_out, or_28_out);
  or or_27 (or_27_out, and_102_out, and_103_out);
  xor xor_20 (xor_20_out[3], xor_12_out, or_29_out);
  or or_28 (or_28_out, and_104_out, and_105_out);
  xor xor_21 (xor_20_out[4], xor_13_out, or_30_out);
  or or_29 (or_29_out, and_106_out, and_107_out);
  xor xor_22 (xor_20_out[5], xor_14_out, or_31_out);
  or or_30 (or_30_out, and_108_out, and_109_out);
  xor xor_23 (xor_20_out[6], xor_15_out, or_32_out);
  or or_31 (or_31_out, and_110_out, and_111_out);
  xor xor_24 (xor_20_out[7], xor_16_out, in_33);
  or or_32 (or_32_out, and_112_out, and_113_out);
  assign controlled_buffer_1_out = in_12 ? xor_20_out : 8'bz;  // Controlled_Buffer controlled_buffer_16
  LED led_1 (.in(xor_20_out[0]));
  Hex_Digit_Display hex_digit_display_7 (.value({xor_20_out[0], xor_20_out[1], xor_20_out[2], xor_20_out[3]}));  // open: dp
  Hex_Digit_Display hex_digit_display_8 (.value({xor_20_out[4], xor_20_out[5], xor_20_out[6], xor_20_out[7]}));  // open: dp
  not not_52 (not_52_out, Write);
  not not_53 (not_53_out, Write);
  not not_54 (not_54_out, Write);
  not not_55 (not_55_out, Write);
  not not_56 (not_56_out, Address_mode);
  and and_114 (and_114_out, nor_49_out, not_52_out);
  and and_115 (and_115_out, Write, undriven_4);
  and and_116 (and_116_out, nor_51_out, not_53_out);
  and and_117 (and_117_out, Write, undriven_3);
  and and_118 (and_118_out, nor_53_out, not_54_out);
  and and_119 (and_119_out, Write, undriven_2);
  and and_120 (and_120_out, nor_55_out, not_55_out);
  and and_121 (and_121_out, Write, undriven);
  and and_122 (and_122_out, in_27, not_56_out);
  and and_123 (and_123_out, nor_49_out, Address_mode);
  and and_124 (and_124_out, in_28, not_56_out);
  and and_125 (and_125_out, nor_51_out, Address_mode);
  and and_126 (and_126_out, in_29, not_56_out);
  and and_127 (and_127_out, nor_53_out, Address_mode);
  and and_128 (and_128_out, in_30, not_56_out);
  and and_129 (and_129_out, nor_55_out, Address_mode);
  or or_33 (or_33_out, and_114_out, and_115_out);
  or or_34 (or_34_out, and_116_out, and_117_out);
  or or_35 (or_35_out, and_118_out, and_119_out);
  or or_36 (or_36_out, and_120_out, and_121_out);
  assign controlled_buffer_1_out = in_4 ? ram_1_dout : 8'bz;  // Controlled_Buffer controlled_buffer_17
  or or_37 (or_37_out[0], and_122_out, and_123_out);
  or or_38 (or_37_out[1], and_124_out, and_125_out);
  or or_39 (or_37_out[2], and_126_out, and_127_out);
  or or_40 (or_37_out[3], and_128_out, and_129_out);
  not not_57 (not_57_out, or_33_out);
  not not_58 (not_58_out, or_34_out);
  not not_59 (not_59_out, or_35_out);
  not not_60 (not_60_out, or_36_out);
  and and_130 (and_130_out, not_57_out, and_1_out);
  and and_131 (and_131_out, and_1_out, or_33_out);
  and and_132 (and_132_out, not_58_out, and_1_out);
  and and_133 (and_133_out, and_1_out, or_34_out);
  and and_134 (and_134_out, not_59_out, and_1_out);
  and and_135 (and_135_out, and_1_out, or_35_out);
  and and_136 (and_136_out, not_60_out, and_1_out);
  and and_137 (and_137_out, and_1_out, or_36_out);
  nor nor_49 (nor_49_out, and_130_out, nor_50_out);
  nor nor_50 (nor_50_out, nor_49_out, and_131_out);
  nor nor_51 (nor_51_out, and_132_out, nor_52_out);
  nor nor_52 (nor_52_out, nor_51_out, and_133_out);
  nor nor_53 (nor_53_out, and_134_out, nor_54_out);
  nor nor_54 (nor_54_out, nor_53_out, and_135_out);
  nor nor_55 (nor_55_out, and_136_out, nor_56_out);
  nor nor_56 (nor_56_out, nor_55_out, and_137_out);
  RAM #(.addrWidth(4)) ram_1 (
    .addr(or_37_out), .we(in_13), .clk(clock_1_out),
    .din({Address, in_25, in_21, in_20, in_19, in_18, in_17, Data}), .dout(ram_1_dout));  // open: oe
endmodule
